# Fritzing sketch ESP-01_LED (saved by Fritzing 0.9.3b)
breadboards: 1

parts:
  LED1 = LEDs [package=led10mm]
  U1 = ESP8266 WiFi Module [part_number=ESP8266]
  VCC1 = Battery
  R2 = Resistor [tolerance=±5% resistance=100 package=THT]

nets:
  N1: LED1.C, R2.Pin_1
  N2: LED1.A, U1.VCC, U1.CH_PD, VCC1.+
  N3: U1.GPIO_0, U1.GPIO_2, R2.Pin_0
  N4: U1.GND, VCC1.-

custom parts:
  ESP8266 WiFi Module: Generic WiFi Module based on the ESP8266 with onboard PCB antenna and UART communications
