# Fritzing sketch NodeMCU_Relay (saved by Fritzing 0.9.3b)
breadboards: 1

parts:
  KY-1 = Keyes Relay [package=THT]
  U1 = NodeMCU V1.0
  LED2 = LEDs [package=led10mm]  # not connected

nets:
  N1: KY-1.signal, U1.D2
  N2: KY-1.power, U1.Vin
  N3: KY-1.ground, U1.GND

notes:
  Esta parte liga na tomada
  (110 ou 220v, dependendo da sua casa e do seu relé)
  Esta parte liga na lâmpada
  (obviamente uma lâmpada de 110 ou 220v, a mesma da sua casa)
  Não custa nada avisar:
  MUITO CUIDADO ao mexer com a eletricidade da sua casa, você pode MORRER!!!
  Veja o projeto completo no canal
  Infortrônica Para Zumbis, no Youtube.
  Aqui você liga em um carregador de celular.

custom parts:
  Keyes Relay: The Keyes 5V relay module is suitable for SCM development, home appliance control. It uses a 5V~12V TIL control signal which can control DC / AC signal.
  NodeMCU V1.0: ESP8266 based NodeMCU
