# Fritzing sketch ESP-01_DHT11 (saved by Fritzing 0.9.3b)
breadboards: 1

parts:
  U1 = ESP8266 WiFi Module [part_number=ESP8266]
  VCC1 = Battery
  R2 = Resistor [tolerance=±5% resistance=4.7k package=THT]
  DHT1 = DHT11 Humitidy and Temperature Sensor

nets:
  VCC: U1.VCC, U1.CH_PD, VCC1.+, R2.Pin_0, DHT1.VDD
  N1: U1.GPIO_2, R2.Pin_1, DHT1.DATA
  GND: U1.GND, U1.TXD, VCC1.-, DHT1.GND

custom parts:
  ESP8266 WiFi Module: Generic WiFi Module based on the ESP8266 with onboard PCB antenna and UART communications
  DHT11 Humitidy and Temperature Sensor: DHT11 Humidity and Temperature Sensor
