# Fritzing sketch ESP-01_FTDI (saved by Fritzing 0.9.3b)

parts:
  U1 = ESP8266 WiFi Module [part_number=ESP8266]
  Componente1 = FTDI Basic Programmer

nets:
  N1: U1.RXD, Componente1.TXO
  N2: U1.VCC, U1.CH_PD, Componente1.POWER
  GND: U1.GPIO_0, U1.GND, Componente1.GND
  N3: U1.TXD, Componente1.RXI

notes:
  Este é o esquema necessário para gravar seu programa no ESP8266, modelo ESP-01.
  Atenção à ligação do GPIO_0 ao GND (fio laranja). Esta ligação é a que permite a gravação do seu programa.
  NÃO alimente o ESP-01 com 5v! Ele deve ser ligado ao 3.3v, senão você QUEIMA o ESP.
  Atenção!
  Algumas versões do FTDI (o vermelhinho aí do esquema) podem não fornecer a corrente necessária para fazer o ESP8266 funcionar (até 200mA).
  Neste caso, alimente o ESP com uma outra fonte de 3.3v que forneça esta corrente.

custom parts:
  ESP8266 WiFi Module: Generic WiFi Module based on the ESP8266 with onboard PCB antenna and UART communications
