# Fritzing sketch NodeMCU_Fita_LED_RGB (saved by Fritzing 0.9.3b)
breadboards: 1

parts:
  R2 = Resistor [tolerance=±5% resistance=470 package=THT]
  R1 = Resistor [tolerance=±5% resistance=470 package=THT]
  R3 = Resistor [tolerance=±5% resistance=470 package=THT]
  Analog_RGB_LED_Strip1 = Analog RGB LED Strip
  Q1 = TIP120 Hi-Current Darlington Transistor
  Q2 = TIP120 Hi-Current Darlington Transistor
  Q3 = TIP120 Hi-Current Darlington Transistor
  U2 = NodeMCU V1.0
  JACK2 = 2.1mm Barrel Jack with Terminal Block
  LM7806 = Voltage Regulator [package=78xxl]
  C5 = Electrolytic Capacitor [capacitance=470µF voltage=10V package="200 mil [THT, electrolytic]"]
  C6 = Electrolytic Capacitor [capacitance=470µF voltage=10V package="200 mil [THT, electrolytic]"]
  C7 = Ceramic Capacitor [capacitance=0.1µF package="200 mil [THT, multilayer]"]
  C8 = Ceramic Capacitor [capacitance=0.1µF package="200 mil [THT, multilayer]"]

nets:
  N1: R2.Pin_0, Q2.BASE
  N2: R2.Pin_1, U2.D6
  N3: R1.Pin_0, U2.D5
  N4: R1.Pin_1, Q1.BASE
  N5: R3.Pin_0, Q3.BASE
  N6: R3.Pin_1, U2.D7
  N7: Analog_RGB_LED_Strip1.12v, JACK2.POS, LM7806.IN, C6.+, C8.0
  N8: Analog_RGB_LED_Strip1.G, Q1.COLLECTOR
  N9: Analog_RGB_LED_Strip1.R, Q2.COLLECTOR
  N10: Analog_RGB_LED_Strip1.B, Q3.COLLECTOR
  GND: Q1.EMITTER, U2.GND, U2.RST, JACK2.NEG, LM7806.GND, C5.-, C6.-, C7.1, C8.1
  N11: U2.Vin, LM7806.OUT, C5.+, C7.0

notes:
  Aqui é a entrada da energia que alimentará a fita e o circuito eletrônico. (12V DC)
  Aqui a tensão foi abaixada pelo regulador para 5V, suficiente para alimentar o NodeMCU.
  Controlando uma fita de LED RGB pelo celular.
  Componentes principais:
  1 NodeMCU;
  1 Fita de LED RGB de qualquer tamanho;
  1 Fonte de alimentação 12V para a fita;
  3 Transistores TIP122 NPN;
  1 CI LM7805;
  2 capacitores cerâmicos de 0.1uF;
  2 capacitores eletrolíticos de 470uF;
  3 Resistores de 470 Ohms;
  Veja detalhes sobre como montar este projeto em:

custom parts:
  Analog RGB LED Strip: Analog RGB LED strip
  NodeMCU V1.0: ESP8266 based NodeMCU
