# Fritzing sketch ReguladorTensao5V (saved by Fritzing 0.9.3b)
circuit board: 3.5cm x 2.4cm
breadboards: 1

parts:
  C1 = Electrolytic Capacitor [capacitance=470µF voltage=10V package="200 mil [THT, electrolytic]"]
  C4 = Ceramic Capacitor [capacitance=0.1µF package="200 mil [THT, multilayer]"]
  C2 = Ceramic Capacitor [capacitance=0.1µF package="200 mil [THT, multilayer]"]
  LM7805 = Voltage Regulator [package=78xxl]
  C3 = Electrolytic Capacitor [capacitance=470µF voltage=10V package="200 mil [THT, electrolytic]"]
  JACK1 = 2.1mm Barrel Jack with Terminal Block
  J1 = Screw terminal - 2 pins [package=THT]

nets:
  N1: C1.-, C4.1, C2.1, LM7805.GND, C3.-, JACK1.NEG, J1.pin1
  N2: C1.+, C2.0, LM7805.IN, JACK1.POS
  N3: C4.0, LM7805.OUT, C3.+, J1.pin2

notes:
  Time Lapse Raspberry, 1.0
  Marco Rabelo - 2015
  V 1.0
  A entrada pode ser entre 8 e 30V DC
  A saída sempre será 5V DC (corrente máxima de 1A)
  Componentes:
  1 CI LM7805;
  2 capacitores cerâmicos de 0.1uF;
  2 capacitores eletrolíticos de 470uF.
