# Fritzing sketch ESP-01_Interruptor_Wifi (saved by Fritzing 0.9.3b)
breadboards: 1

parts:
  part = ESP8266 WiFi Module [part_number=ESP8266]
  part_2 = Resistor [tolerance=±5% resistance=3.3k package="1206 [SMD]"]
  Interruptor = Round Pushbutton
  part_3 = Battery
  part_4 = Resistor [tolerance=±5% resistance=3.3k package="1206 [SMD]"]
  100nF = Capacitor [package=cap-pth-small2]

nets:
  N1: part.VCC, part.CH_PD, part_2.Pin_1, part_3.+, part_4.Pin_1, 100nF.1
  N2: part.GPIO_0, Interruptor.leg0, part_4.Pin_0
  N3: part.GPIO_2, part_2.Pin_0, Interruptor.leg1
  N4: part.GND, part_3.-, 100nF.2

notes:
  ESP8266, versão ESP-01, funcionando como interruptor wifi.
  Principais componentes:
  1 ESP-01;
  1 Fonte de alimentação que forneça 3,3V (duas pilhas AA, por exemplo);
  2 Resistores de 3,3k;
  1 Capacitor cerâmico de 100nF (número 104);
  1 Interruptor (qualquer um que atenda sua necessidade)
  Veja detalhes sobre como montar este projeto no canal Infortrônica Para Zumbis, no Youtube.

custom parts:
  ESP8266 WiFi Module: Generic WiFi Module based on the ESP8266 with onboard PCB antenna and UART communications
