# Fritzing sketch ESP01_Relé (saved by Fritzing 0.9.3b)

parts:
  part = ESP8266 WiFi Module [part_number=ESP8266]
  Transistor_2N2222 = TRANSISTOR_NPN_2 [package=to-92]
  Módulo_Relé_5V = Keyes Relay [package=THT]
  Módulo_AMS1117_ou_LD1117 = V_REG_LD1117VXX [package=78xxl]
  part_2 = Resistor [tolerance=±5% resistance=1k package="1206 [SMD]"]
  part_3 = Resistor [tolerance=±5% resistance=47k package="1206 [SMD]"]
  HLK-PM1 = HLK-PM01
  100nF = Capacitor [package=cap-pth-small2]
  LED3 = LEDs [package=led10mm]

nets:
  N1: part.VCC, part.CH_PD, Módulo_AMS1117_ou_LD1117.OUT, 100nF.1
  N2: part.GPIO_2, part_3.Pin_0
  GND: part.GND, Transistor_2N2222.C, Módulo_Relé_5V.ground, Módulo_AMS1117_ou_LD1117.GND, HLK-PM1.-Vo, 100nF.2
  N3: Transistor_2N2222.B, part_3.Pin_1
  N4: Transistor_2N2222.E, Módulo_Relé_5V.signal, part_2.Pin_0
  N5: Módulo_Relé_5V.power, Módulo_AMS1117_ou_LD1117.IN, part_2.Pin_1, HLK-PM1.+Vo
  N6: Módulo_Relé_5V.NO, LED3.A

notes:
  Aqui liga na rede elétrica da sua casa.
  Aqui vai na rede elétrica.
  (110 ou 220v, dependendo da sua casa e do seu relé)
  Esta parte liga na lâmpada
  (obviamente uma lâmpada de 110 ou 220v, a mesma da sua casa)
  Não custa nada avisar:
  MUITO CUIDADO ao mexer com a eletricidade da sua casa, você pode MORRER!!!
  ESP8266, versão ESP-01, controlando relé
  Principais componentes:
  1 ESP-01;
  1 Fonte Hi-Link KLK-PM1 (ou qualquer fonte de 5V);
  1 Módulo stepdown AMS1117 ou LD1117;
  1 Transistor 2N2222 (ou qualquer NPN equivalente);
  1 Capacitor cerâmico de 100nF (número 104);
  1 Resistor de 1k;
  1 Resistor de 47k;
  1 Módulo relé de 5V;
  Veja detalhes sobre como montar este projeto no canal Infortrônica Para Zumbis, no Youtube.

custom parts:
  ESP8266 WiFi Module: Generic WiFi Module based on the ESP8266 with onboard PCB antenna and UART communications
  Keyes Relay: The Keyes 5V relay module is suitable for SCM development, home appliance control. It uses a 5V~12V TIL control signal which can control DC / AC signal.
